# Fritzing sketch schemaCircuitiTreCondensatori (saved by Fritzing 0.8.7b)
breadboards: 1

parts:
  Componente1 = Arduino Uno (Rev3)
  R1 = Resistor [tolerance=±5% resistance=100 package=THT]
  R2 = Resistor [tolerance=±5% resistance=10k package=THT]
  R3 = Resistor [tolerance=±5% resistance=10k package=THT]
  C1 = Electrolytic Capacitor [capacitance=330µF package="100 mil [THT, electrolytic]"]
  C2 = Electrolytic Capacitor [capacitance=100µF package="100 mil [THT, electrolytic]"]
  C3 = Electrolytic Capacitor [capacitance=22µF package="100 mil [THT, electrolytic]"]

nets:
  N1: Componente1.A0, R1.Pin_1, C1.+
  N2: Componente1.A1, R2.Pin_1, C2.+
  N3: Componente1.A2, R3.Pin_1, C3.+
  N4: Componente1.D13/SCK, R1.Pin_0, R2.Pin_0, R3.Pin_0
  N5: Componente1.GND, C1.-, C2.-, C3.-
